# Fritzing sketch New HUB SD TFT PCB to SKR v1.3 (saved by Fritzing 0.9.3b)
circuit board: 4cm x 5.5cm
breadboards: 1

parts:
  J1 = male pin header, 6 pins [form="♂ (male)"]
  J3 = male pin header, 5 pins [form="♂ (male)"]
  J2 = male pin header, 5 pins [form="♂ (male)"]
  J4 = male pin header, 2 pins [form="♂ (male)"]
  J5 = male pin header, 2 pins [form="♂ (male)"]
  J6 = male pin header, 2 pins [form="♂ (male)"]
  J7 = male pin header, 9 pins [form="♂ (male)"]
  J8 = male pin header, 10 pins [form="♂ (male)"]

nets:
  N1: J1.pin1, J7.pin1
  N2: J1.pin2, J7.pin2
  N3: J1.pin3, J7.pin3
  N4: J1.pin4, J7.pin4
  N5: J1.pin5, J7.pin5
  N6: J1.pin6, J7.pin6
  N7: J3.pin1, J7.pin7
  N8: J3.pin2, J7.pin8
  N9: J3.pin3, J7.pin9
  N10: J3.pin4, J8.pin1
  N11: J3.pin5, J8.pin2
  N12: J2.pin1, J4.pin1, J6.pin1, J6.pin2, J8.pin10
  N13: J2.pin2, J8.pin6
  N14: J2.pin3, J8.pin5
  N15: J2.pin4, J8.pin4
  N16: J2.pin5, J8.pin3
  N17: J4.pin2, J8.pin9
  N18: J5.pin1, J8.pin7
  N19: J5.pin2, J8.pin8

notes:
  D19|D18|D15|D14|D2|D3
  GND|5V
  GND|GND
  A14|A13
  TRIGORILLA SIDE
  RST|D41|D51|D53|D52
  GND|D49|D33|D31|D50
  EXTERNAL DEVICES SIDE
  D53
  D52
  D50
  D31
  D33
  D49
  A14
  A13
  +5V
  GND
  D19
  D18
  D15
  D14
  D2
  D3
  RST
  D41
  D51
